# Fritzing sketch esp_hookup (saved by Fritzing 0.9.2b)
breadboards: 1

parts:
  Part1 = Arduino Uno (Rev3)
  Part2 = LSM303 Breakout Board - Tilt-Compensated Compass

nets:
  N1: Part1.D10_PWM/SS, Part2.VCC
  N2: Part1.D11_PWM/MOSI, Part2.SCL_M
  N3: Part1.D4, Part2.SDA_M
  N4: Part1.3V3, Part2.SA0
  N5: Part1.GND, Part2.INT1

notes:
  esp
