# Fritzing sketch circuit (saved by Fritzing 0.9.2b)
breadboards: 1

parts:
  Part1 = Arduino Uno (Rev3)
  LED1 = LED - 5mm [color="Red (633nm)" package="5 mm [THT]"]
  R1 = Resistor [tolerance=±0.05% resistance=100 package=THT]

nets:
  N1: Part1.GND, R1.Pin_0
  N2: Part1.D4, LED1.anode
  N3: LED1.cathode, R1.Pin_1

notes:
  Resistor should be 100 Ohm or more
