# Fritzing sketch circuit (saved by Fritzing 0.9.2b)
breadboards: 1

parts:
  Part1 = Arduino Uno (Rev3)
  part = Photocell (LDR) [package=THT]
  R1 = Resistor [tolerance=±5% resistance=10k package=THT]

nets:
  N1: Part1.A0, part.pin_0, R1.Pin_0
  N2: Part1.5V, part.pin_1
  N3: Part1.GND, R1.Pin_1

notes:
  Resistor should be 10k Ohm
