# Fritzing sketch vippebryter_hookup (saved by Fritzing 0.9.2b)
breadboards: 1

parts:
  Part1 = Arduino Uno (Rev3)
  S1 = Toggle Switch [package=THT]

nets:
  N1: Part1.GND, S1.COM
  N2: Part1.D2, S1.L2
  N3: Part1.D3_PWM, S1.L1
